// Logisim project control-logic.circ as structural Verilog: 1 circuit, main circuit control_logic
module control_logic (
  input  [31:0] Instruction,
  input  BrEq,
  input  BrLt,
  output PCSel,
  output RegWEn,
  output [2:0] ImmSel,
  output BrUn,
  output ASel,
  output BSel,
  output [3:0] ALUSel,
  output MemWEn,
  output [1:0] WBSel
);

  wire and_1_out, and_2_out, and_3_out, and_4_out, and_5_out, and_6_out, and_7_out, comparator_1_eq,
       comparator_2_eq, comparator_3_eq, comparator_4_eq, comparator_5_eq, comparator_6_eq, comparator_7_eq,
       comparator_8_eq, comparator_9_eq, comparator_10_eq, comparator_11_eq, comparator_12_eq,
       comparator_13_eq, comparator_14_eq, comparator_15_eq, comparator_16_eq, comparator_17_eq,
       comparator_18_eq, comparator_19_eq, comparator_20_eq, comparator_21_eq, comparator_22_eq,
       comparator_23_eq, comparator_24_eq, comparator_25_eq, comparator_26_eq, comparator_27_eq,
       comparator_28_eq, comparator_29_eq, comparator_30_eq, comparator_31_eq, comparator_32_eq,
       comparator_33_eq, comparator_34_eq, comparator_35_eq, comparator_36_eq, comparator_37_eq,
       comparator_38_eq, comparator_39_eq, comparator_40_eq, comparator_41_eq, comparator_42_eq,
       comparator_43_eq, comparator_44_eq, comparator_45_eq, not_1_out, not_2_out, not_3_out, or_1_out;
  wire [5:0] ROM_Input;
  wire [15:14] rom_1_data;

  Comparator #(.mode("unsigned"), .width(17)) comparator_1 (
    .a({Instruction[6:0], Instruction[14:12], Instruction[31:25]}), .b(17'hcc01), .eq(comparator_1_eq));  // open: gt, lt
  Comparator #(.mode("unsigned"), .width(17)) comparator_2 (
    .a({Instruction[6:0], Instruction[14:12], Instruction[31:25]}), .b(17'hcc20), .eq(comparator_2_eq));  // open: gt, lt
  Comparator #(.mode("unsigned"), .width(17)) comparator_3 (
    .a({Instruction[6:0], Instruction[14:12], Instruction[31:25]}), .b(17'hcc80), .eq(comparator_3_eq));  // open: gt, lt
  Comparator #(.mode("unsigned"), .width(17)) comparator_4 (
    .a({Instruction[6:0], Instruction[14:12], Instruction[31:25]}), .b(17'hcc81), .eq(comparator_4_eq));  // open: gt, lt
  Comparator #(.mode("unsigned"), .width(17)) comparator_5 (
    .a({Instruction[6:0], Instruction[14:12], Instruction[31:25]}), .b(17'hcd81), .eq(comparator_5_eq));  // open: gt, lt
  Comparator #(.mode("unsigned"), .width(17)) comparator_6 (
    .a({Instruction[6:0], Instruction[14:12], Instruction[31:25]}), .b(17'hcd00), .eq(comparator_6_eq));  // open: gt, lt
  Comparator #(.mode("unsigned"), .width(17)) comparator_7 (
    .a({Instruction[6:0], Instruction[14:12], Instruction[31:25]}), .b(17'hce00), .eq(comparator_7_eq));  // open: gt, lt
  Comparator #(.mode("unsigned"), .width(17)) comparator_8 (
    .a({Instruction[6:0], Instruction[14:12], Instruction[31:25]}), .b(17'hce80), .eq(comparator_8_eq));  // open: gt, lt
  Comparator #(.mode("unsigned"), .width(17)) comparator_9 (
    .a({Instruction[6:0], Instruction[14:12], Instruction[31:25]}), .b(17'hcea0), .eq(comparator_9_eq));  // open: gt, lt
  Comparator #(.mode("unsigned"), .width(17)) comparator_10 (
    .a({Instruction[6:0], Instruction[14:12], Instruction[31:25]}), .b(17'hcf00), .eq(comparator_10_eq));  // open: gt, lt
  Comparator #(.mode("unsigned"), .width(17)) comparator_11 (
    .a({Instruction[6:0], Instruction[14:12], Instruction[31:25]}), .b(17'hcf80), .eq(comparator_11_eq));  // open: gt, lt
  Comparator #(.mode("unsigned"), .width(10)) comparator_12 (
    .a({Instruction[6:0], Instruction[14:12]}), .b(10'h18), .eq(comparator_12_eq));  // open: gt, lt
  Comparator #(.mode("unsigned"), .width(10)) comparator_13 (
    .a({Instruction[6:0], Instruction[14:12]}), .b(10'h19), .eq(comparator_13_eq));  // open: gt, lt
  Comparator #(.mode("unsigned"), .width(10)) comparator_14 (
    .a({Instruction[6:0], Instruction[14:12]}), .b(10'h1a), .eq(comparator_14_eq));  // open: gt, lt
  Comparator #(.mode("unsigned"), .width(10)) comparator_15 (
    .a({Instruction[6:0], Instruction[14:12]}), .b(10'h98), .eq(comparator_15_eq));  // open: gt, lt
  Comparator #(.mode("unsigned"), .width(17)) comparator_16 (
    .a({Instruction[6:0], Instruction[14:12], Instruction[31:25]}), .b(17'h4c80), .eq(comparator_16_eq));  // open: gt, lt
  Comparator #(.mode("unsigned"), .width(10)) comparator_17 (
    .a({Instruction[6:0], Instruction[14:12]}), .b(10'h9a), .eq(comparator_17_eq));  // open: gt, lt
  Comparator #(.mode("unsigned"), .width(10)) comparator_18 (
    .a({Instruction[6:0], Instruction[14:12]}), .b(10'h9c), .eq(comparator_18_eq));  // open: gt, lt
  Comparator #(.mode("unsigned"), .width(17)) comparator_19 (
    .a({Instruction[6:0], Instruction[14:12], Instruction[31:25]}), .b(17'h4e80), .eq(comparator_19_eq));  // open: gt, lt
  Comparator #(.mode("unsigned"), .width(17)) comparator_20 (
    .a({Instruction[6:0], Instruction[14:12], Instruction[31:25]}), .b(17'h4ea0), .eq(comparator_20_eq));  // open: gt, lt
  Comparator #(.mode("unsigned"), .width(10)) comparator_21 (
    .a({Instruction[6:0], Instruction[14:12]}), .b(10'h9e), .eq(comparator_21_eq));  // open: gt, lt
  Comparator #(.mode("unsigned"), .width(10)) comparator_22 (
    .a({Instruction[6:0], Instruction[14:12]}), .b(10'h9f), .eq(comparator_22_eq));  // open: gt, lt
  Comparator #(.mode("unsigned"), .width(10)) comparator_23 (
    .a({Instruction[6:0], Instruction[14:12]}), .b(10'h118), .eq(comparator_23_eq));  // open: gt, lt
  Comparator #(.mode("unsigned"), .width(10)) comparator_24 (
    .a({Instruction[6:0], Instruction[14:12]}), .b(10'h119), .eq(comparator_24_eq));  // open: gt, lt
  Comparator #(.mode("unsigned"), .width(10)) comparator_25 (
    .a({Instruction[6:0], Instruction[14:12]}), .b(10'h11a), .eq(comparator_25_eq));  // open: gt, lt
  Comparator #(.mode("unsigned"), .width(10)) comparator_26 (
    .a({Instruction[6:0], Instruction[14:12]}), .b(10'h318), .eq(comparator_26_eq));  // open: gt, lt
  Comparator #(.mode("unsigned"), .width(10)) comparator_27 (
    .a({Instruction[6:0], Instruction[14:12]}), .b(10'h319), .eq(comparator_27_eq));  // open: gt, lt
  Comparator #(.mode("unsigned"), .width(10)) comparator_28 (
    .a({Instruction[6:0], Instruction[14:12]}), .b(10'h31c), .eq(comparator_28_eq));  // open: gt, lt
  Comparator #(.mode("unsigned"), .width(10)) comparator_29 (
    .a({Instruction[6:0], Instruction[14:12]}), .b(10'h31d), .eq(comparator_29_eq));  // open: gt, lt
  Comparator #(.mode("unsigned"), .width(10)) comparator_30 (
    .a({Instruction[6:0], Instruction[14:12]}), .b(10'h31e), .eq(comparator_30_eq));  // open: gt, lt
  Comparator #(.mode("unsigned"), .width(10)) comparator_31 (
    .a({Instruction[6:0], Instruction[14:12]}), .b(10'h31f), .eq(comparator_31_eq));  // open: gt, lt
  ROM #(.addrWidth(6), .dataWidth(16)) rom_1 (
    .addr(ROM_Input), .data({rom_1_data, WBSel, MemWEn, ALUSel, BSel, ASel, BrUn, ImmSel, RegWEn}));
  Comparator #(.mode("unsigned"), .width(17)) comparator_32 (
    .a({Instruction[6:0], Instruction[14:12], Instruction[31:25]}), .b(17'hcc00), .eq(comparator_32_eq));  // open: gt, lt
  Comparator #(.mode("unsigned"), .width(7)) comparator_33 (
    .a(Instruction[6:0]), .b(7'b0010111), .eq(comparator_33_eq));  // open: gt, lt
  Comparator #(.mode("unsigned"), .width(7)) comparator_34 (
    .a(Instruction[6:0]), .b(7'b0110111), .eq(comparator_34_eq));  // open: gt, lt
  Comparator #(.mode("unsigned"), .width(7)) comparator_35 (
    .a(Instruction[6:0]), .b(7'b1101111), .eq(comparator_35_eq));  // open: gt, lt
  Comparator #(.mode("unsigned"), .width(10)) comparator_36 (
    .a({Instruction[6:0], Instruction[14:12]}), .b(10'h338), .eq(comparator_36_eq));  // open: gt, lt
  Comparator #(.mode("unsigned"), .width(7)) comparator_37 (
    .a(Instruction[6:0]), .b(7'b1100011), .eq(comparator_37_eq));  // open: gt, lt
  Comparator #(.mode("unsigned"), .width(3)) comparator_38 (
    .a(Instruction[14:12]), .b(3'b000), .eq(comparator_38_eq));  // open: gt, lt
  not not_1 (not_1_out, BrEq);
  Comparator #(.mode("unsigned"), .width(3)) comparator_39 (
    .a(Instruction[14:12]), .b(3'b001), .eq(comparator_39_eq));  // open: gt, lt
  Comparator #(.mode("unsigned"), .width(3)) comparator_40 (
    .a(Instruction[14:12]), .b(3'b100), .eq(comparator_40_eq));  // open: gt, lt
  not not_2 (not_2_out, BrLt);
  Comparator #(.mode("unsigned"), .width(3)) comparator_41 (
    .a(Instruction[14:12]), .b(3'b101), .eq(comparator_41_eq));  // open: gt, lt
  Comparator #(.mode("unsigned"), .width(3)) comparator_42 (
    .a(Instruction[14:12]), .b(3'b110), .eq(comparator_42_eq));  // open: gt, lt
  not not_3 (not_3_out, BrLt);
  Comparator #(.mode("unsigned"), .width(3)) comparator_43 (
    .a(Instruction[14:12]), .b(3'b111), .eq(comparator_43_eq));  // open: gt, lt
  and and_1 (and_1_out, BrEq, comparator_38_eq);
  and and_2 (and_2_out, not_1_out, comparator_39_eq);
  and and_3 (and_3_out, BrLt, comparator_40_eq);
  and and_4 (and_4_out, not_2_out, comparator_41_eq);
  and and_5 (and_5_out, BrLt, comparator_42_eq);
  and and_6 (and_6_out, not_3_out, comparator_43_eq);
  or or_1 (or_1_out, and_1_out, and_2_out, and_3_out, and_4_out, and_5_out, and_6_out);
  and and_7 (and_7_out, comparator_37_eq, or_1_out);
  Comparator #(.mode("unsigned"), .width(7)) comparator_44 (
    .a(Instruction[6:0]), .b(7'b1101111), .eq(comparator_44_eq));  // open: gt, lt
  Comparator #(.mode("unsigned"), .width(7)) comparator_45 (
    .a(Instruction[6:0]), .b(7'b1100111), .eq(comparator_45_eq));  // open: gt, lt
  or or_2 (PCSel, and_7_out, comparator_44_eq, comparator_45_eq);
  Priority_Encoder #(.select_enc(6)) priority_encoder_1 (
    .in0(comparator_32_eq), .in1(comparator_1_eq), .in2(comparator_2_eq), .in3(comparator_3_eq),
    .in4(comparator_4_eq), .in5(comparator_5_eq), .in6(comparator_6_eq), .in7(comparator_7_eq),
    .in8(comparator_8_eq), .in9(comparator_9_eq), .in10(comparator_10_eq), .in11(comparator_11_eq),
    .in12(comparator_12_eq), .in13(comparator_13_eq), .in14(comparator_14_eq), .in15(comparator_15_eq),
    .in16(comparator_16_eq), .in17(comparator_17_eq), .in18(comparator_18_eq), .in19(comparator_19_eq),
    .in20(comparator_20_eq), .in21(comparator_21_eq), .in22(comparator_22_eq), .in23(comparator_23_eq),
    .in24(comparator_24_eq), .in25(comparator_25_eq), .in26(comparator_26_eq), .in27(comparator_27_eq),
    .in28(comparator_28_eq), .in29(comparator_29_eq), .in30(comparator_30_eq), .in31(comparator_31_eq),
    .in32(comparator_33_eq), .in33(comparator_34_eq), .in34(comparator_35_eq), .in35(comparator_36_eq),
    .out(ROM_Input));  // open: in36, in37, in38, in39, in40, in41, in42, in43, in44, in45, in46, in47, in48, in49, in50, in51, in52, in53, in54, in55, in56, in57, in58, in59, in60, in61, in62, in63, gs, en_out, en_in

  // Other names for the same wires on the sheet: func7[6:0] = Instruction[31:25];
  //   opcode_func3_func7[16:0] = {Instruction[6:0], Instruction[14:12], Instruction[31:25]};
  //   func3[2:0] = Instruction[14:12]; opcode_func3[9:0] = {Instruction[6:0], Instruction[14:12]};
  //   opcode[6:0] = Instruction[6:0]

  // Notes on the sheet:
  //   INPUTS to your circuit
  //   Connect ROM Input here ->
  //   contents of rom_1 (hex, n*v repeats v):
  //   1001 1401 1601 1081 1481 1581 1101 1201 1281 1681 1301 1381 41 41 41 1041 10c1 1141 1241 12c1 16c1
  //   1341 13c1 842 842 842 4*64 74 74 1067 17e7 2069 2041 10 18 11 19 100 20 101 21 110 22 111 23 1000 24
  //   1001 25 1010 26 1011 27 1100 28 1101 29 1110 30 1111 31
  //   ROM FOR CONTROL LOGIC
  //   DON'T CHANGE THE LOCATIONS OF THE INPUTS AND OUTPUTS!
  //   This is only if you choose to do the ROM option
  //   OUTPUT from your circuit
  //   Reminder: If using ROM, use combinational logic for PCSel
endmodule
