// Logisim project cpu2.circ as structural Verilog: 1 circuit, main circuit cpu
module cpu (
  input  clk,
  input  [31:0] Instruction,
  input  [31:0] MemReadData,
  output [31:0] MemAddress,
  output [31:0] ProgramCounter,
  output [31:0] ra,
  output [31:0] sp,
  output [31:0] t0,
  output [31:0] t1,
  output [31:0] t2,
  output [31:0] s0,
  output [31:0] s1,
  output [31:0] a0,
  output [3:0] MemWriteMask,
  output [31:0] MemWriteData
);

  wire ASel, BrEq, BrLt, BrUn, BSel, MemWEn, PCSel, RegWEn;
  wire [1:0] WBSel;
  wire [2:0] ImmSel;
  wire [3:0] ALUSel;
  wire [31:0] DataToReg, immediate, Instruction_p2, multiplexer_1_out, multiplexer_2_out, multiplexer_3_out,
       multiplexer_4_out, multiplexer_5_out, pc_4, pc_4_p2, ProgramCounter_p2, ReadData2, regfile_1_readdata1;

  Register #(.width(32)) register_1 (.D(multiplexer_1_out), .clk(clk), .Q(Instruction_p2));  // open: en, clr
  Multiplexer #(.width(32)) multiplexer_1 (.in0(Instruction), .in1(32'h13), .out(multiplexer_1_out), .sel(PCSel));
  Adder #(.width(32)) adder_1 (.a(ProgramCounter), .b(32'h4), .out(pc_4));  // open: cin, cout
  Multiplexer #(.width(32)) multiplexer_2 (.in0(pc_4), .in1(MemAddress), .out(multiplexer_2_out), .sel(PCSel));
  control_logic control_logic_1 (
    .Instruction(Instruction_p2), .BrEq(BrEq), .BrLt(BrLt), .PCSel(PCSel), .RegWEn(RegWEn), .ImmSel(ImmSel),
    .BrUn(BrUn), .ASel(ASel), .BSel(BSel), .ALUSel(ALUSel), .MemWEn(MemWEn), .WBSel(WBSel));
  Register #(.width(32)) PC (.D(multiplexer_2_out), .clk(clk), .Q(ProgramCounter));  // open: en, clr
  Multiplexer #(.width(32)) multiplexer_3 (.in0(ReadData2), .in1(immediate), .out(multiplexer_3_out), .sel(BSel));
  imm_gen imm_gen_1 (.Instruction(Instruction_p2), .ImmSel(ImmSel), .Immediate(immediate));
  Register #(.width(32)) register_2 (.D(ProgramCounter), .clk(clk), .Q(ProgramCounter_p2));  // open: en, clr
  alu alu_1 (.A(multiplexer_4_out), .B(multiplexer_3_out), .ALUSel(ALUSel), .ALUResult(MemAddress));
  Multiplexer #(.width(32)) multiplexer_4 (
    .in0(regfile_1_readdata1), .in1(ProgramCounter_p2), .out(multiplexer_4_out), .sel(ASel));
  Adder #(.width(32)) adder_2 (.a(ProgramCounter_p2), .b(32'h4), .out(pc_4_p2));  // open: cin, cout
  Multiplexer #(.select(2), .width(32)) multiplexer_5 (
    .in0(DataToReg), .in1(MemAddress), .in2(pc_4_p2), .out(multiplexer_5_out), .sel(WBSel));  // open: in3
  regfile regfile_1 (
    .ReadIndex1(Instruction_p2[19:15]), .ReadIndex2(Instruction_p2[24:20]),
    .WriteIndex(Instruction_p2[11:7]), .WriteData(multiplexer_5_out), .RegWEn(RegWEn), .clk(clk), .ra(ra),
    .sp(sp), .t0(t0), .t1(t1), .t2(t2), .s0(s0), .s1(s1), .a0(a0), .ReadData1(regfile_1_readdata1),
    .ReadData2(ReadData2));
  branch_comp branch_comp_1 (.BrData1(regfile_1_readdata1), .BrData2(ReadData2), .BrUn(BrUn), .BrEq(BrEq), .BrLt(BrLt));
  partial_store partial_store_1 (
    .Instruction(Instruction_p2), .MemAddress(MemAddress), .DataFromReg(ReadData2), .MemWEn(MemWEn),
    .MemWriteMask(MemWriteMask), .DataToMem(MemWriteData));
  partial_load partial_load_1 (
    .Instruction(Instruction_p2), .MemAddress(MemAddress), .DataFromMem(MemReadData), .DataToReg(DataToReg));

  // Other names for the same wires on the sheet: ALUResult[31:0] = MemAddress

  // Notes on the sheet:
  //   To IMEM
  //   IMEM (do **NOT** move this)
  //   From IMEM
  //   Inputs/Outputs for testing. Do **NOT** move these.
  //   It is OK to move the PC, RegFile, ALU, MEM, Branch Comp, Imm Gen, Partial Load, Partial Store and Control Logic to wherever is most convenient for you when constructing your CPU, and to delete this text
  //   To DMEM
  //   DMEM (do **NOT** move this)
  //   From DMEM
endmodule
