// Logisim project partial-store.circ as structural Verilog: 1 circuit, main circuit partial_store
module partial_store (
  input  [31:0] Instruction,
  input  [31:0] MemAddress,
  input  [31:0] DataFromReg,
  input  MemWEn,
  output [3:0] MemWriteMask,
  output [31:0] DataToMem
);

  wire [3:0] multiplexer_3_out, x0mask, x1mask;
  wire [31:0] multiplexer_8_out, x0, x1;

  Multiplexer #(.select(2), .width(4)) multiplexer_1 (
    .in0(4'b0001), .in1(4'b0010), .in2(4'b0100), .in3(4'b1000), .out(x0mask), .sel(MemAddress[1:0]));
  Multiplexer #(.select(2), .width(4)) multiplexer_2 (
    .in0(4'b0011), .in2(4'b1100), .out(x1mask), .sel(MemAddress[1:0]));  // open: in1, in3
  Multiplexer #(.select(3), .width(4)) multiplexer_3 (
    .in0(x0mask), .in1(x1mask), .in2(4'b1111), .out(multiplexer_3_out), .sel(Instruction[14:12]));  // open: in3, in4, in5, in6, in7
  Multiplexer #(.select(2), .width(32)) multiplexer_4 (
    .in0({{24{1'b0}}, DataFromReg[7:0]}), .in1({{16{1'b0}}, DataFromReg[7:0], {8{1'b0}}}),
    .in2({{8{1'b0}}, DataFromReg[7:0], {16{1'b0}}}), .in3({DataFromReg[7:0], {24{1'b0}}}), .out(x0),
    .sel(MemAddress[1:0]));
  Multiplexer #(.select(2), .width(32)) multiplexer_5 (
    .in0({{16{1'b0}}, DataFromReg[15:0]}), .in2({DataFromReg[15:0], {16{1'b0}}}), .out(x1),
    .sel(MemAddress[1:0]));  // open: in1, in3
  Multiplexer #(.width(4)) multiplexer_6 (.in0(4'b0000), .in1(multiplexer_3_out), .out(MemWriteMask), .sel(MemWEn));
  Multiplexer #(.width(32)) multiplexer_7 (.in0({32{1'b0}}), .in1(multiplexer_8_out), .out(DataToMem), .sel(MemWEn));
  Multiplexer #(.select(3), .width(32)) multiplexer_8 (
    .in0(x0), .in1(x1), .in2(DataFromReg), .out(multiplexer_8_out), .sel(Instruction[14:12]));  // open: in3, in4, in5, in6, in7

  // Other names for the same wires on the sheet: f3[2:0] = Instruction[14:12]; bot2[1:0] = MemAddress[1:0];
  //   x0b00[7:0] = DataFromReg[7:0]; x0b01[15:8] = DataFromReg[7:0]; x0b10[23:16] = DataFromReg[7:0];
  //   x0b11[31:24] = DataFromReg[7:0]; x1b00[15:0] = DataFromReg[15:0]; x1b10[31:16] = DataFromReg[15:0]

  // Notes on the sheet:
  //   INPUTS to your circuit
  //   DON'T CHANGE THE LOCATIONS OF THE INPUTS AND OUTPUTS!
  //   OUTPUT from your circuit
endmodule
