// Logisim project regfile.circ as structural Verilog: 1 circuit, main circuit regfile
module regfile (
  input  [4:0] ReadIndex1,
  input  [4:0] ReadIndex2,
  input  [4:0] WriteIndex,
  input  [31:0] WriteData,
  input  RegWEn,
  input  clk,
  output [31:0] ra,
  output [31:0] sp,
  output [31:0] t0,
  output [31:0] t1,
  output [31:0] t2,
  output [31:0] s0,
  output [31:0] s1,
  output [31:0] a0,
  output [31:0] ReadData1,
  output [31:0] ReadData2
);

  wire RegWEn0, RegWEn1, RegWEn2, RegWEn3, RegWEn4, RegWEn5, RegWEn6, RegWEn7, RegWEn8, RegWEn9, RegWEn10,
       RegWEn11, RegWEn12, RegWEn13, RegWEn14, RegWEn15, RegWEn16, RegWEn17, RegWEn18, RegWEn19, RegWEn20,
       RegWEn21, RegWEn22, RegWEn23, RegWEn24, RegWEn25, RegWEn26, RegWEn27, RegWEn28, RegWEn29, RegWEn30,
       RegWEn31;
  wire [31:0] a1, a2, a3, a4, a5, a6, a7, gp, s2, s3, s4, s5, s6, s7, s8, s9, s10, s11, t3, t4, t5, t6, tp,
       Wa1, Wa2, Wa3, Wa4, Wa5, Wa6, Wa7, Wa8, Wa9, Wa10, Wa11, Wa12, Wa13, Wa14, Wa15, Wa16, Wa17, Wa18,
       Wa19, Wa20, Wa21, Wa22, Wa23, Wa24, Wa25, Wa26, Wa27, Wa28, Wa29, Wa30, Wa31, x0;

  Register #(.width(32)) register_1 (.D({32{1'b0}}), .en(RegWEn0), .clk(clk), .Q(x0));  // open: clr
  Register #(.width(32)) register_2 (.D(Wa1), .en(RegWEn1), .clk(clk), .Q(ra));  // open: clr
  Register #(.width(32)) register_3 (.D(Wa2), .en(RegWEn2), .clk(clk), .Q(sp));  // open: clr
  Register #(.width(32)) register_4 (.D(Wa9), .en(RegWEn9), .clk(clk), .Q(s1));  // open: clr
  Register #(.width(32)) register_5 (.D(Wa10), .en(RegWEn10), .clk(clk), .Q(a0));  // open: clr
  Register #(.width(32)) register_6 (.D(Wa17), .en(RegWEn17), .clk(clk), .Q(a7));  // open: clr
  Register #(.width(32)) register_7 (.D(Wa18), .en(RegWEn18), .clk(clk), .Q(s2));  // open: clr
  Register #(.width(32)) register_8 (.D(Wa19), .en(RegWEn19), .clk(clk), .Q(s3));  // open: clr
  Register #(.width(32)) register_9 (.D(Wa20), .en(RegWEn20), .clk(clk), .Q(s4));  // open: clr
  Register #(.width(32)) register_10 (.D(Wa3), .en(RegWEn3), .clk(clk), .Q(gp));  // open: clr
  Register #(.width(32)) register_11 (.D(Wa4), .en(RegWEn4), .clk(clk), .Q(tp));  // open: clr
  Register #(.width(32)) register_12 (.D(Wa11), .en(RegWEn11), .clk(clk), .Q(a1));  // open: clr
  Register #(.width(32)) register_13 (.D(Wa12), .en(RegWEn12), .clk(clk), .Q(a2));  // open: clr
  Register #(.width(32)) register_14 (.D(Wa21), .en(RegWEn21), .clk(clk), .Q(s5));  // open: clr
  Register #(.width(32)) register_15 (.D(Wa22), .en(RegWEn22), .clk(clk), .Q(s6));  // open: clr
  Register #(.width(32)) register_16 (.D(Wa23), .en(RegWEn23), .clk(clk), .Q(s7));  // open: clr
  // Register #(.width(32)) register_17: pin names not known; wires that end beside it: Wa24, RegWEn24, clk, s8
  Demultiplexer #(.select(5)) demultiplexer_1 (
    .out0(RegWEn0), .out1(RegWEn1), .out2(RegWEn2), .out3(RegWEn3), .out4(RegWEn4), .out5(RegWEn5),
    .out6(RegWEn6), .out7(RegWEn7), .out8(RegWEn8), .out9(RegWEn9), .out10(RegWEn10), .out11(RegWEn11),
    .out12(RegWEn12), .out13(RegWEn13), .out14(RegWEn14), .out15(RegWEn15), .out16(RegWEn16),
    .out17(RegWEn17), .out18(RegWEn18), .out19(RegWEn19), .out20(RegWEn20), .out21(RegWEn21),
    .out22(RegWEn22), .out23(RegWEn23), .out24(RegWEn24), .out25(RegWEn25), .out26(RegWEn26),
    .out27(RegWEn27), .out28(RegWEn28), .out29(RegWEn29), .out30(RegWEn30), .out31(RegWEn31), .in(RegWEn),
    .sel(WriteIndex));
  Register #(.width(32)) register_18 (.D(Wa5), .en(RegWEn5), .clk(clk), .Q(t0));  // open: clr
  Register #(.width(32)) register_19 (.D(Wa6), .en(RegWEn6), .clk(clk), .Q(t1));  // open: clr
  Register #(.width(32)) register_20 (.D(Wa13), .en(RegWEn13), .clk(clk), .Q(a3));  // open: clr
  Register #(.width(32)) register_21 (.D(Wa14), .en(RegWEn14), .clk(clk), .Q(a4));  // open: clr
  Register #(.width(32)) register_22 (.D(Wa25), .en(RegWEn25), .clk(clk), .Q(s9));  // open: clr
  Register #(.width(32)) register_23 (.D(Wa26), .en(RegWEn26), .clk(clk), .Q(s10));  // open: clr
  Register #(.width(32)) register_24 (.D(Wa27), .en(RegWEn27), .clk(clk), .Q(s11));  // open: clr
  Register #(.width(32)) register_25 (.D(Wa28), .en(RegWEn28), .clk(clk), .Q(t3));  // open: clr
  Register #(.width(32)) register_26 (.D(Wa7), .en(RegWEn7), .clk(clk), .Q(t2));  // open: clr
  Register #(.width(32)) register_27 (.D(Wa8), .en(RegWEn8), .clk(clk), .Q(s0));  // open: clr
  Register #(.width(32)) register_28 (.D(Wa15), .en(RegWEn15), .clk(clk), .Q(a5));  // open: clr
  Register #(.width(32)) register_29 (.D(Wa16), .en(RegWEn16), .clk(clk), .Q(a6));  // open: clr
  Register #(.width(32)) register_30 (.D(Wa29), .en(RegWEn29), .clk(clk), .Q(t4));  // open: clr
  Register #(.width(32)) register_31 (.D(Wa30), .en(RegWEn30), .clk(clk), .Q(t5));  // open: clr
  Register #(.width(32)) register_32 (.D(Wa31), .en(RegWEn31), .clk(clk), .Q(t6));  // open: clr
  Demultiplexer #(.select(5), .width(32)) demultiplexer_2 (
    .out1(Wa1), .out2(Wa2), .out3(Wa3), .out4(Wa4), .out5(Wa5), .out6(Wa6), .out7(Wa7), .out8(Wa8),
    .out9(Wa9), .out10(Wa10), .out11(Wa11), .out12(Wa12), .out13(Wa13), .out14(Wa14), .out15(Wa15),
    .out16(Wa16), .out17(Wa17), .out18(Wa18), .out19(Wa19), .out20(Wa20), .out21(Wa21), .out22(Wa22),
    .out23(Wa23), .out24(Wa24), .out25(Wa25), .out26(Wa26), .out27(Wa27), .out28(Wa28), .out29(Wa29),
    .out30(Wa30), .out31(Wa31), .in(WriteData), .sel(WriteIndex));  // open: out0
  Multiplexer #(.select(5), .width(32)) multiplexer_1 (
    .in0(x0), .in1(ra), .in2(sp), .in3(gp), .in4(tp), .in5(t0), .in6(t1), .in7(t2), .in8(s0), .in9(s1),
    .in10(a0), .in11(a1), .in12(a2), .in13(a3), .in14(a4), .in15(a5), .in16(a6), .in17(a7), .in18(s2),
    .in19(s3), .in20(s4), .in21(s5), .in22(s6), .in23(s7), .in24(s8), .in25(s9), .in26(s10), .in27(s11),
    .in28(t3), .in29(t4), .in30(t5), .in31(t6), .out(ReadData1), .sel(ReadIndex1));
  Multiplexer #(.select(5), .width(32)) multiplexer_2 (
    .in0(x0), .in1(ra), .in2(sp), .in3(gp), .in4(tp), .in5(t0), .in6(t1), .in7(t2), .in8(s0), .in9(s1),
    .in10(a0), .in11(a1), .in12(a2), .in13(a3), .in14(a4), .in15(a5), .in16(a6), .in17(a7), .in18(s2),
    .in19(s3), .in20(s4), .in21(s5), .in22(s6), .in23(s7), .in24(s8), .in25(s9), .in26(s10), .in27(s11),
    .in28(t3), .in29(t4), .in30(t5), .in31(t6), .out(ReadData2), .sel(ReadIndex2));

  // Notes on the sheet:
  //   INPUTS to your circuit
  //   DON'T CHANGE THE LOCATIONS OF THE INPUTS AND OUTPUTS!
  //   These are DEBUG/TEST outputs from your circuit.
  //   OUTPUTS from your circuit
endmodule
